# Fritzing sketch Sketch (saved by Fritzing 0.9.3b)
breadboards: 1

parts:
  Matrix_keypad1 = KEYPAD 4x4
  Part2 = Arduino Mega 2560 (Rev3)
  U1 = LCD-16X2 [package=lcd-16x2]
  J1 = Piezo Speaker
  SPKR1 = Loudspeaker
  U2 = POT [package=pot_alpha_rv16af-20]
  MOTOR1 = 28BYJ-48 Stepper Motor
  ULN2003A_-_Stepper_Driver_Board1 = ULN2003A - Stepper Driver Board [package=board]
  U3 = ESP8266 WiFi Module [part_number=ESP8266]
  R1 = Resistor [tolerance=±5% resistance=220 package=THT]
  LED1 = smd LED [color="Red (633nm)" package="0805 [SMD]"]
  LED3 = smd LED [color="Green (555nm)" package="0805 [SMD]"]
  LED4 = smd LED [color="Blue (470nm)" package="0805 [SMD]"]
  R2 = Resistor [tolerance=±5% resistance=220 package=THT]
  R3 = Resistor [tolerance=±5% resistance=220 package=THT]

nets:
  N1: Matrix_keypad1.col1, Part2.D1_TX0
  N2: Matrix_keypad1.col2, Part2.D2_PWM
  N3: Matrix_keypad1.col3, Part2.D3_PWM
  N4: Matrix_keypad1.col4, Part2.D4_PWM
  N5: Matrix_keypad1.row1, Part2.D5_PWM
  N6: Matrix_keypad1.row2, Part2.D6_PWM
  N7: Matrix_keypad1.row3, Part2.D7_PWM
  N8: Matrix_keypad1.row4, Part2.D8_PWM
  N9: Part2.A0, U1.RS
  N10: Part2.A1, U1.E
  N11: Part2.A2, U1.DB4
  N12: Part2.A3, U1.DB5
  N13: Part2.A4, U1.DB6
  N14: Part2.A5, U1.DB7
  N15: Part2.D17_PWM/RX2, U3.TXD
  N16: Part2.D16_PWM/TX2, U3.RXD
  N17: Part2.D10_PWM, SPKR1.pin2
  3V3: Part2.3V3, U3.VCC
  5V: Part2.5V, U1.VDD, U1.A, U2.E, ULN2003A_-_Stepper_Driver_Board1.VCC
  GND: Part2.GND, U1.VSS, U1.R_W, U1.K, J1.pin1, SPKR1.pin1, U2.A, ULN2003A_-_Stepper_Driver_Board1.GND, U3.GND, LED1.cathode, LED3.cathode, LED4.cathode
  N18: Part2.D25, ULN2003A_-_Stepper_Driver_Board1.IN1
  N19: Part2.D27, ULN2003A_-_Stepper_Driver_Board1.IN2
  N20: Part2.D29, ULN2003A_-_Stepper_Driver_Board1.IN3
  N21: Part2.D31, ULN2003A_-_Stepper_Driver_Board1.IN4
  N22: Part2.D37, R2.Pin_1
  N23: Part2.D45, R1.Pin_1
  N24: Part2.D49, J1.pin2
  N25: Part2.D53, R3.Pin_1
  N26: U1.VO, U2.S
  N27: MOTOR1.RED, ULN2003A_-_Stepper_Driver_Board1.RED
  N28: MOTOR1.ORANGE, ULN2003A_-_Stepper_Driver_Board1.ORANGE
  N29: MOTOR1.YELLOW, ULN2003A_-_Stepper_Driver_Board1.YELLOW
  N30: MOTOR1.PINK, ULN2003A_-_Stepper_Driver_Board1.PINK
  N31: MOTOR1.BLUE, ULN2003A_-_Stepper_Driver_Board1.BLUE
  N32: ULN2003A_-_Stepper_Driver_Board1.IN7, ULN2003A_-_Stepper_Driver_Board1.B, ULN2003A_-_Stepper_Driver_Board1.C, ULN2003A_-_Stepper_Driver_Board1.D, ULN2003A_-_Stepper_Driver_Board1.E, ULN2003A_-_Stepper_Driver_Board1.G
  N33: R1.Pin_0, LED1.anode
  N34: LED3.anode, R2.Pin_0
  N35: LED4.anode, R3.Pin_0

custom parts:
  KEYPAD 4x4: Matrix keypad 16 buttons, 4 rows x 4 columns
  ULN2003A - Stepper Driver Board: A common stepper motor driver board based on ULN2003APG darlington array
  ESP8266 WiFi Module: Generic WiFi Module based on the ESP8266 with onboard PCB antenna and UART communications
